# Fritzing sketch BlackPill_nRF24_Tx (saved by Fritzing 0.9.9b)
breadboards: 1

parts:
  M1 = STM32F103C8T6 blue mini board
  Part1 = NRF24L01+ Breakout Board  # not connected
  Part2 = FTDI Basic Programmer  # not connected
  DS1 = DS18B20 1-Wire Temperature Sensor [part_number=DS18B20]
  DS2 = DS18B20 1-Wire Temperature Sensor [part_number=DS18B20]

nets:
  N1: M1.B14, M1.B0
  N2: M1.A11, M1.B11
  N3: M1.B3, M1.A5
  N4: M1.B5, DS1.DQ, DS2.DQ
  N5: M1.B9, M1.B1
  GND: M1.G, M1.GND, DS1.GND, DS2.GND
  VDD: DS1.VDD, DS2.VDD
